// Logisim project Subtractor.circ as structural Verilog: 3 circuits, main circuit main
module main (
  input  [31:0] A,
  input  [31:0] B,
  output [31:0] S
);

  wire n8_bit_1_d8, n8_bit_2_d8, n8_bit_3_d8;

  _8_bit u_8_bit_1 (
    .d(1'b0), .a0(A[0]), .b0(B[0]), .a1(A[1]), .b1(B[1]), .a2(A[2]), .b2(B[2]), .a3(A[3]), .b3(B[3]),
    .a4(A[4]), .b4(B[4]), .a5(A[5]), .b5(B[5]), .a6(A[6]), .b6(B[6]), .a7(A[7]), .b7(B[7]), .s0(S[0]),
    .s1(S[1]), .s2(S[2]), .s3(S[3]), .s4(S[4]), .s5(S[5]), .s6(S[6]), .s7(S[7]), .d8(n8_bit_1_d8));
  _8_bit u_8_bit_2 (
    .d(n8_bit_1_d8), .a0(A[8]), .b0(B[8]), .a1(A[9]), .b1(B[9]), .a2(A[10]), .b2(B[10]), .a3(A[11]),
    .b3(B[11]), .a4(A[12]), .b4(B[12]), .a5(A[13]), .b5(B[13]), .a6(A[14]), .b6(B[14]), .a7(A[15]),
    .b7(B[15]), .s0(S[8]), .s1(S[9]), .s2(S[10]), .s3(S[11]), .s4(S[12]), .s5(S[13]), .s6(S[14]), .s7(S[15]),
    .d8(n8_bit_2_d8));
  _8_bit u_8_bit_3 (
    .d(n8_bit_2_d8), .a0(A[16]), .b0(B[16]), .a1(A[17]), .b1(B[17]), .a2(A[18]), .b2(B[18]), .a3(A[19]),
    .b3(B[19]), .a4(A[20]), .b4(B[20]), .a5(A[21]), .b5(B[21]), .a6(A[22]), .b6(B[22]), .a7(A[23]),
    .b7(B[23]), .s0(S[16]), .s1(S[17]), .s2(S[18]), .s3(S[19]), .s4(S[20]), .s5(S[21]), .s6(S[22]),
    .s7(S[23]), .d8(n8_bit_3_d8));
  _8_bit u_8_bit_4 (
    .d(n8_bit_3_d8), .a0(A[24]), .b0(B[24]), .a1(A[25]), .b1(B[25]), .a2(A[26]), .b2(B[26]), .a3(A[27]),
    .b3(B[27]), .a4(A[28]), .b4(B[28]), .a5(A[29]), .b5(B[29]), .a6(A[30]), .b6(B[30]), .a7(A[31]),
    .b7(B[31]), .s0(S[24]), .s1(S[25]), .s2(S[26]), .s3(S[27]), .s4(S[28]), .s5(S[29]), .s6(S[30]), .s7(S[31]));  // open: d8
endmodule

module _8_bit (
  input  d,
  input  a0,
  input  b0,
  input  a1,
  input  b1,
  input  a2,
  input  b2,
  input  a3,
  input  b3,
  input  a4,
  input  b4,
  input  a5,
  input  b5,
  input  a6,
  input  b6,
  input  a7,
  input  b7,
  output s0,
  output s1,
  output s2,
  output s3,
  output s4,
  output s5,
  output s6,
  output s7,
  output d8
);

  wire n1_bit_1_d1, n1_bit_2_d1, n1_bit_3_d1, n1_bit_4_d1, n1_bit_5_d1, n1_bit_6_d1, n1_bit_7_d1;

  _1_bit u_1_bit_1 (.a1(a0), .b1(b0), .d0(d), .c1(s0), .d1(n1_bit_1_d1));
  _1_bit u_1_bit_2 (.a1(a1), .b1(b1), .d0(n1_bit_1_d1), .c1(s1), .d1(n1_bit_2_d1));
  _1_bit u_1_bit_3 (.a1(a2), .b1(b2), .d0(n1_bit_2_d1), .c1(s2), .d1(n1_bit_3_d1));
  _1_bit u_1_bit_4 (.a1(a3), .b1(b3), .d0(n1_bit_3_d1), .c1(s3), .d1(n1_bit_4_d1));
  _1_bit u_1_bit_5 (.a1(a4), .b1(b4), .d0(n1_bit_4_d1), .c1(s4), .d1(n1_bit_5_d1));
  _1_bit u_1_bit_6 (.a1(a5), .b1(b5), .d0(n1_bit_5_d1), .c1(s5), .d1(n1_bit_6_d1));
  _1_bit u_1_bit_7 (.a1(a6), .b1(b6), .d0(n1_bit_6_d1), .c1(s6), .d1(n1_bit_7_d1));
  _1_bit u_1_bit_8 (.a1(a7), .b1(b7), .d0(n1_bit_7_d1), .c1(s7), .d1(d8));
endmodule

module _1_bit (
  input  a1,
  input  b1,
  input  d0,
  output c1,
  output d1
);

  wire and_1_out, and_2_out, and_3_out, and_4_out, and_5_out, and_6_out, and_7_out, not_1_out, not_2_out,
       not_3_out;

  not not_1 (not_1_out, a1);
  not not_2 (not_2_out, b1);
  not not_3 (not_3_out, d0);
  and and_1 (and_1_out, not_1_out, not_2_out, d0);
  and and_2 (and_2_out, not_1_out, b1, not_3_out);
  and and_3 (and_3_out, a1, not_2_out, not_3_out);
  and and_4 (and_4_out, a1, b1, d0);
  and and_5 (and_5_out, not_1_out, d0);
  and and_6 (and_6_out, not_1_out, b1);
  and and_7 (and_7_out, b1, d0);
  or or_1 (c1, and_1_out, and_2_out, and_3_out, and_4_out);
  or or_2 (d1, and_5_out, and_6_out, and_7_out);
endmodule
