// Logisim project mips-lite-noprobe.circ as structural Verilog: 7 circuits, main circuit main
module main (
  input  IFUreset,
  input  DMreset,
  input  RFreset
);

  wire alu_1_zero, ALUSrc, Clock_out, controller_1_memtoreg, controller_1_memwrite, controller_1_npc_sel,
       RegDst, RegWrite;
  wire [1:0] controller_1_aluctr_1_0, ExtOp;
  wire [4:0] multiplexer_1_out;
  wire [31:0] alu_1_result, dm_1_out_6, ext_1__32, gpr_1_rd1, gpr_1_rd2, ifu_1_instr_31_0, multiplexer_2_out,
       multiplexer_3_out;

  Clock Clock (.out(Clock_out));
  IFU ifu_1 (
    .IfBeq(controller_1_npc_sel), .Zero(alu_1_zero), .Instr_31_0(ifu_1_instr_31_0), .CLK(Clock_out),
    .Reset(IFUreset));
  Multiplexer #(.width(5)) multiplexer_1 (
    .in0(ifu_1_instr_31_0[20:16]), .in1(ifu_1_instr_31_0[15:11]), .out(multiplexer_1_out), .sel(RegDst));  // open: en
  Controller controller_1 (
    .funct(ifu_1_instr_31_0[5:0]), .Opcode(ifu_1_instr_31_0[31:26]), .ResDst(RegDst), .ALUSrc(ALUSrc),
    .MemtoReg(controller_1_memtoreg), .RegWrite(RegWrite), .MemWrite(controller_1_memwrite),
    .nPC_sel(controller_1_npc_sel), .ExtOp(ExtOp), .ALUCtr_1_0(controller_1_aluctr_1_0));
  EXT ext_1 (.imm16(ifu_1_instr_31_0[15:0]), ._32(ext_1__32), .ExtOp(ExtOp));
  GPR gpr_1 (
    .RegWrite(RegWrite), .A1(ifu_1_instr_31_0[25:21]), .A2(ifu_1_instr_31_0[20:16]), .A3(multiplexer_1_out),
    .WD(multiplexer_3_out), .RD1(gpr_1_rd1), .RD2(gpr_1_rd2), .clock(Clock_out), .Reset(RFreset));
  Multiplexer #(.width(32)) multiplexer_2 (
    .in0(gpr_1_rd2), .in1(ext_1__32), .out(multiplexer_2_out), .sel(ALUSrc));  // open: en
  ALU alu_1 (
    .ALUOp_1_0(controller_1_aluctr_1_0), .Data1(gpr_1_rd1), .Data2(multiplexer_2_out), .Result(alu_1_result),
    .Zero(alu_1_zero));
  DM dm_1 (
    .in_1(alu_1_result[6:2]), .in_2(gpr_1_rd2), .out_6(dm_1_out_6), .MemWrite(controller_1_memwrite),
    .clock(Clock_out), .reset(DMreset));
  Multiplexer #(.width(32)) multiplexer_3 (
    .in0(alu_1_result), .in1(dm_1_out_6), .out(multiplexer_3_out), .sel(controller_1_memtoreg));  // open: en
endmodule

module Controller (
  input  [5:0] funct,
  input  [5:0] Opcode,
  output ResDst,
  output ALUSrc,
  output MemtoReg,
  output RegWrite,
  output MemWrite,
  output nPC_sel,
  output [1:0] ExtOp,
  output [1:0] ALUCtr_1_0
);

  wire addu_out, lw_out, not_1_out, not_2_out, not_3_out, not_4_out, not_5_out, not_6_out, not_7_out,
       not_8_out, not_9_out, not_10_out, not_11_out, not_12_out, ori_out, subu_out;

  not not_1 (not_1_out, funct[5]);
  not not_2 (not_2_out, funct[3]);
  not not_3 (not_3_out, funct[4]);
  not not_4 (not_4_out, funct[2]);
  not not_5 (not_5_out, funct[1]);
  not not_6 (not_6_out, funct[0]);
  not not_7 (not_7_out, Opcode[5]);
  not not_8 (not_8_out, Opcode[3]);
  not not_9 (not_9_out, Opcode[4]);
  not not_10 (not_10_out, Opcode[1]);
  not not_11 (not_11_out, Opcode[2]);
  not not_12 (not_12_out, Opcode[0]);
  and ori (ori_out, not_7_out, not_9_out, Opcode[3], Opcode[2], not_10_out, Opcode[0]);
  and addu (addu_out, funct[5], not_3_out, not_2_out, not_4_out, not_5_out, funct[0], not_7_out, not_9_out, not_8_out, not_11_out, not_10_out, not_12_out);
  and subu (subu_out, funct[5], not_3_out, not_2_out, not_4_out, funct[1], funct[0], not_7_out, not_9_out, not_8_out, not_11_out, not_10_out, not_12_out);
  and lw (lw_out, Opcode[5], not_9_out, not_8_out, not_11_out, Opcode[1], Opcode[0]);
  and sw (MemWrite, Opcode[5], not_9_out, Opcode[3], not_11_out, Opcode[1], Opcode[0]);
  and beq (nPC_sel, not_7_out, not_9_out, not_8_out, Opcode[2], not_10_out, not_12_out);
  and lui (ExtOp[1], not_7_out, not_9_out, Opcode[3], Opcode[2], Opcode[1], Opcode[0]);
  or u_ResDst (ResDst, addu_out, subu_out);
  or u_ALUSrc (ALUSrc, ori_out, lw_out, MemWrite, ExtOp[1]);
  buf u_MemtoReg (MemtoReg, lw_out);  // OR_Gate
  or u_RegWrite (RegWrite, addu_out, subu_out, ori_out, lw_out, ExtOp[1]);
  or ExtOp0 (ExtOp[0], lw_out, MemWrite);
  buf ALUCtr1 (ALUCtr_1_0[1], ori_out);  // OR_Gate
  or ALUCtr0 (ALUCtr_1_0[0], subu_out, nPC_sel);

  // Notes on the sheet:
  //   ExtOp1
endmodule

module GPR (
  input  RegWrite,
  input  clock,
  input  [4:0] A1,
  input  [4:0] A2,
  input  [31:0] WD,
  input  [4:0] A3,
  input  Reset,
  output [31:0] RD1,
  output [31:0] RD2
);

  wire demultiplexer_2_out0, demultiplexer_2_out1, demultiplexer_2_out2, demultiplexer_2_out3,
       demultiplexer_2_out4, demultiplexer_2_out5, demultiplexer_2_out6, demultiplexer_2_out7,
       demultiplexer_2_out8, demultiplexer_2_out9, demultiplexer_2_out10, demultiplexer_2_out11,
       demultiplexer_2_out12, demultiplexer_2_out13, demultiplexer_2_out14, demultiplexer_2_out15,
       demultiplexer_2_out16, demultiplexer_2_out17, demultiplexer_2_out18, demultiplexer_2_out19,
       demultiplexer_2_out20, demultiplexer_2_out21, demultiplexer_2_out22, demultiplexer_2_out23,
       demultiplexer_2_out24, demultiplexer_2_out25, demultiplexer_2_out26, demultiplexer_2_out27,
       demultiplexer_2_out28, demultiplexer_2_out29, demultiplexer_2_out30, demultiplexer_2_out31;
  wire [31:0] demultiplexer_1_out0, demultiplexer_1_out1, demultiplexer_1_out2, demultiplexer_1_out3,
       demultiplexer_1_out4, demultiplexer_1_out5, demultiplexer_1_out6, demultiplexer_1_out7,
       demultiplexer_1_out8, demultiplexer_1_out9, demultiplexer_1_out10, demultiplexer_1_out11,
       demultiplexer_1_out12, demultiplexer_1_out13, demultiplexer_1_out14, demultiplexer_1_out15,
       demultiplexer_1_out16, demultiplexer_1_out17, demultiplexer_1_out18, demultiplexer_1_out19,
       demultiplexer_1_out20, demultiplexer_1_out21, demultiplexer_1_out22, demultiplexer_1_out23,
       demultiplexer_1_out24, demultiplexer_1_out25, demultiplexer_1_out26, demultiplexer_1_out27,
       demultiplexer_1_out28, demultiplexer_1_out29, demultiplexer_1_out30, demultiplexer_1_out31,
       main_1_out_67, main_1_out_68, main_1_out_69, main_1_out_70, main_1_out_71, main_1_out_72,
       main_1_out_73, main_1_out_74, main_1_out_75, main_1_out_76, main_1_out_77, main_1_out_78,
       main_1_out_79, main_1_out_80, main_1_out_81, main_1_out_82, main_1_out_83, main_1_out_84,
       main_1_out_85, main_1_out_86, main_1_out_87, main_1_out_88, main_1_out_89, main_1_out_90,
       main_1_out_91, main_1_out_92, main_1_out_93, main_1_out_94, main_1_out_95, main_1_out_96,
       main_1_out_97, main_1_out_98;

  Demultiplexer #(.select(5), .width(32)) demultiplexer_1 (
    .out0(demultiplexer_1_out0), .out1(demultiplexer_1_out1), .out2(demultiplexer_1_out2),
    .out3(demultiplexer_1_out3), .out4(demultiplexer_1_out4), .out5(demultiplexer_1_out5),
    .out6(demultiplexer_1_out6), .out7(demultiplexer_1_out7), .out8(demultiplexer_1_out8),
    .out9(demultiplexer_1_out9), .out10(demultiplexer_1_out10), .out11(demultiplexer_1_out11),
    .out12(demultiplexer_1_out12), .out13(demultiplexer_1_out13), .out14(demultiplexer_1_out14),
    .out15(demultiplexer_1_out15), .out16(demultiplexer_1_out16), .out17(demultiplexer_1_out17),
    .out18(demultiplexer_1_out18), .out19(demultiplexer_1_out19), .out20(demultiplexer_1_out20),
    .out21(demultiplexer_1_out21), .out22(demultiplexer_1_out22), .out23(demultiplexer_1_out23),
    .out24(demultiplexer_1_out24), .out25(demultiplexer_1_out25), .out26(demultiplexer_1_out26),
    .out27(demultiplexer_1_out27), .out28(demultiplexer_1_out28), .out29(demultiplexer_1_out29),
    .out30(demultiplexer_1_out30), .out31(demultiplexer_1_out31), .in(WD), .sel(A3));  // open: en
  Demultiplexer #(.select(5)) demultiplexer_2 (
    .out0(demultiplexer_2_out0), .out1(demultiplexer_2_out1), .out2(demultiplexer_2_out2),
    .out3(demultiplexer_2_out3), .out4(demultiplexer_2_out4), .out5(demultiplexer_2_out5),
    .out6(demultiplexer_2_out6), .out7(demultiplexer_2_out7), .out8(demultiplexer_2_out8),
    .out9(demultiplexer_2_out9), .out10(demultiplexer_2_out10), .out11(demultiplexer_2_out11),
    .out12(demultiplexer_2_out12), .out13(demultiplexer_2_out13), .out14(demultiplexer_2_out14),
    .out15(demultiplexer_2_out15), .out16(demultiplexer_2_out16), .out17(demultiplexer_2_out17),
    .out18(demultiplexer_2_out18), .out19(demultiplexer_2_out19), .out20(demultiplexer_2_out20),
    .out21(demultiplexer_2_out21), .out22(demultiplexer_2_out22), .out23(demultiplexer_2_out23),
    .out24(demultiplexer_2_out24), .out25(demultiplexer_2_out25), .out26(demultiplexer_2_out26),
    .out27(demultiplexer_2_out27), .out28(demultiplexer_2_out28), .out29(demultiplexer_2_out29),
    .out30(demultiplexer_2_out30), .out31(demultiplexer_2_out31), .in(RegWrite), .sel(A3));  // open: en
  gpr_main main_1 (
    .in_1(demultiplexer_1_out0), .in_2(demultiplexer_1_out1), .in_4(demultiplexer_2_out0),
    .in_5(demultiplexer_2_out1), .in_7(demultiplexer_1_out2), .in_8(demultiplexer_1_out3),
    .in_9(demultiplexer_2_out2), .in_10(demultiplexer_2_out3), .in_11(demultiplexer_1_out4),
    .in_12(demultiplexer_1_out5), .in_13(demultiplexer_2_out4), .in_14(demultiplexer_2_out5),
    .in_15(demultiplexer_1_out6), .in_16(demultiplexer_1_out7), .in_17(demultiplexer_2_out6),
    .in_18(demultiplexer_2_out7), .in_19(demultiplexer_1_out8), .in_20(demultiplexer_1_out9),
    .in_21(demultiplexer_2_out8), .in_22(demultiplexer_2_out9), .in_23(demultiplexer_1_out10),
    .in_24(demultiplexer_1_out11), .in_25(demultiplexer_2_out10), .in_26(demultiplexer_2_out11),
    .in_27(demultiplexer_1_out12), .in_28(demultiplexer_1_out13), .in_29(demultiplexer_2_out12),
    .in_30(demultiplexer_2_out13), .in_31(demultiplexer_1_out14), .in_32(demultiplexer_1_out15),
    .in_33(demultiplexer_2_out14), .in_34(demultiplexer_2_out15), .in_35(demultiplexer_1_out16),
    .in_36(demultiplexer_1_out17), .in_37(demultiplexer_2_out16), .in_38(demultiplexer_2_out17),
    .in_39(demultiplexer_1_out18), .in_40(demultiplexer_1_out19), .in_41(demultiplexer_2_out18),
    .in_42(demultiplexer_2_out19), .in_43(demultiplexer_1_out20), .in_44(demultiplexer_1_out21),
    .in_45(demultiplexer_2_out20), .in_46(demultiplexer_2_out21), .in_47(demultiplexer_1_out22),
    .in_48(demultiplexer_1_out23), .in_49(demultiplexer_2_out22), .in_50(demultiplexer_2_out23),
    .in_51(demultiplexer_1_out24), .in_52(demultiplexer_1_out25), .in_53(demultiplexer_2_out24),
    .in_54(demultiplexer_2_out25), .in_55(demultiplexer_1_out26), .in_56(demultiplexer_1_out27),
    .in_57(demultiplexer_2_out26), .in_58(demultiplexer_2_out27), .in_59(demultiplexer_1_out28),
    .in_60(demultiplexer_1_out29), .in_61(demultiplexer_2_out28), .in_62(demultiplexer_2_out29),
    .in_63(demultiplexer_1_out30), .in_64(demultiplexer_1_out31), .in_65(demultiplexer_2_out30),
    .in_66(demultiplexer_2_out31), .out_67(main_1_out_67), .out_68(main_1_out_68), .out_69(main_1_out_69),
    .out_70(main_1_out_70), .out_71(main_1_out_71), .out_72(main_1_out_72), .out_73(main_1_out_73),
    .out_74(main_1_out_74), .out_75(main_1_out_75), .out_76(main_1_out_76), .out_77(main_1_out_77),
    .out_78(main_1_out_78), .out_79(main_1_out_79), .out_80(main_1_out_80), .out_81(main_1_out_81),
    .out_82(main_1_out_82), .out_83(main_1_out_83), .out_84(main_1_out_84), .out_85(main_1_out_85),
    .out_86(main_1_out_86), .out_87(main_1_out_87), .out_88(main_1_out_88), .out_89(main_1_out_89),
    .out_90(main_1_out_90), .out_91(main_1_out_91), .out_92(main_1_out_92), .out_93(main_1_out_93),
    .out_94(main_1_out_94), .out_95(main_1_out_95), .out_96(main_1_out_96), .out_97(main_1_out_97),
    .out_98(main_1_out_98), .clock(clock), .reset(Reset));
  Multiplexer #(.select(5), .width(32)) multiplexer_1 (
    .in0(main_1_out_67), .in1(main_1_out_68), .in2(main_1_out_69), .in3(main_1_out_70), .in4(main_1_out_71),
    .in5(main_1_out_72), .in6(main_1_out_73), .in7(main_1_out_74), .in8(main_1_out_75), .in9(main_1_out_76),
    .in10(main_1_out_77), .in11(main_1_out_78), .in12(main_1_out_79), .in13(main_1_out_80),
    .in14(main_1_out_81), .in15(main_1_out_82), .in16(main_1_out_83), .in17(main_1_out_84),
    .in18(main_1_out_85), .in19(main_1_out_86), .in20(main_1_out_87), .in21(main_1_out_88),
    .in22(main_1_out_89), .in23(main_1_out_90), .in24(main_1_out_91), .in25(main_1_out_92),
    .in26(main_1_out_93), .in27(main_1_out_94), .in28(main_1_out_95), .in29(main_1_out_96),
    .in30(main_1_out_97), .in31(main_1_out_98), .out(RD1), .sel(A1));  // open: en
  Multiplexer #(.select(5), .width(32)) multiplexer_2 (
    .in0(main_1_out_67), .in1(main_1_out_68), .in2(main_1_out_69), .in3(main_1_out_70), .in4(main_1_out_71),
    .in5(main_1_out_72), .in6(main_1_out_73), .in7(main_1_out_74), .in8(main_1_out_75), .in9(main_1_out_76),
    .in10(main_1_out_77), .in11(main_1_out_78), .in12(main_1_out_79), .in13(main_1_out_80),
    .in14(main_1_out_81), .in15(main_1_out_82), .in16(main_1_out_83), .in17(main_1_out_84),
    .in18(main_1_out_85), .in19(main_1_out_86), .in20(main_1_out_87), .in21(main_1_out_88),
    .in22(main_1_out_89), .in23(main_1_out_90), .in24(main_1_out_91), .in25(main_1_out_92),
    .in26(main_1_out_93), .in27(main_1_out_94), .in28(main_1_out_95), .in29(main_1_out_96),
    .in30(main_1_out_97), .in31(main_1_out_98), .out(RD2), .sel(A2));  // open: en
endmodule

module IFU (
  input  IfBeq,
  input  Zero,
  input  CLK,
  input  Reset,
  output [31:0] Instr_31_0
);

  wire and_1_out;
  wire [29:0] bit_extender_1_out, multiplexer_1_out, n30_bit_1_out_3, n30_bit_2_out_3, PC_q;

  and and_1 (and_1_out, IfBeq, Zero);
  Multiplexer #(.width(30)) multiplexer_1 (
    .in0(n30_bit_1_out_3), .in1(n30_bit_2_out_3), .out(multiplexer_1_out), .sel(and_1_out));  // open: en
  Register #(.width(30), .trigger("falling")) PC (.D(multiplexer_1_out), .Q(PC_q), .clk(CLK), .clr(Reset));  // open: en
  assign bit_extender_1_out = {{14{Instr_31_0[15]}}, Instr_31_0[15:0]};  // Bit_Extender bit_extender_1
  _30_bit u_30_bit_1 (.in_1(30'h1), .in_2(PC_q), .out_3(n30_bit_1_out_3));
  _30_bit u_30_bit_2 (.in_1(bit_extender_1_out), .in_2(n30_bit_1_out_3), .out_3(n30_bit_2_out_3));
  ROM #(.addrWidth(5), .dataWidth(32)) rom_1 (.addr(PC_q[4:0]), .data(Instr_31_0));  // open: sel

  // Other names for the same wires on the sheet: Offset[15:0] = Instr_31_0[15:0]
endmodule

module DM (
  input  [4:0] in_1,
  input  [31:0] in_2,
  input  MemWrite,
  input  clock,
  input  reset,
  output [31:0] out_6
);

  RAM #(.addrWidth(5), .dataWidth(32), .bus("separate")) ram_1 (
    .addr(in_1), .din(in_2), .data(out_6), .str(MemWrite), .clk(clock), .clr(reset));  // open: sel, ld
endmodule

module ALU (
  input  [1:0] ALUOp_1_0,
  input  [31:0] Data1,
  input  [31:0] Data2,
  output [31:0] Result,
  output Zero
);

  wire [31:0] add_s, Or_out, sub_s;

  \修改前Adder_main  add (.A(Data1), .B(Data2), .S(add_s));
  Subtractor_main sub (.A(Data1), .B(Data2), .S(sub_s));
  assign Or_out = Data1 | Data2;  // OR_Gate Or, 32 bits wide
  Comparator #(.width(32)) comparator_1 (.a(Data1), .b(Data2), .eq(Zero));  // open: gt, lt
  Multiplexer #(.select(2), .width(32)) multiplexer_1 (
    .in0(add_s), .in1(sub_s), .in2(Or_out), .out(Result), .sel(ALUOp_1_0));  // open: in3, en
endmodule

module EXT (
  input  [1:0] ExtOp,
  input  [15:0] imm16,
  output [31:0] _32
);

  wire [31:0] bit_extender_1_out, bit_extender_2_out;

  assign bit_extender_1_out = {{16{1'b0}}, imm16};  // Bit_Extender bit_extender_1
  assign bit_extender_2_out = {{16{imm16[15]}}, imm16};  // Bit_Extender bit_extender_2
  Multiplexer #(.select(2), .width(32)) multiplexer_1 (
    .in0(bit_extender_1_out), .in1(bit_extender_2_out), .in2({imm16, {16{1'b0}}}), .out(_32), .sel(ExtOp));  // open: in3, en
endmodule
