// Logisim project 修改前Adder.circ as structural Verilog: 5 circuits, main circuit main
module main (
  input  [31:0] A,
  input  [31:0] B,
  output [31:0] S
);

  wire n8_bit_1_c8, n8_bit_2_c8, n8_bit_3_c8;

  _8_bit u_8_bit_1 (
    .C0(1'b0), .A0(A[0]), .B0(B[0]), .A1(A[1]), .B1(B[1]), .A2(A[2]), .B2(B[2]), .A3(A[3]), .B3(B[3]),
    .A4(A[4]), .B4(B[4]), .A5(A[5]), .B5(B[5]), .A6(A[6]), .B6(B[6]), .A7(A[7]), .B7(B[7]), .S0(S[0]),
    .S1(S[1]), .S2(S[2]), .S3(S[3]), .S4(S[4]), .S5(S[5]), .S6(S[6]), .S7(S[7]), .C8(n8_bit_1_c8));
  _8_bit u_8_bit_2 (
    .C0(n8_bit_1_c8), .A0(A[8]), .B0(B[8]), .A1(A[9]), .B1(B[9]), .A2(A[10]), .B2(B[10]), .A3(A[11]),
    .B3(B[11]), .A4(A[12]), .B4(B[12]), .A5(A[13]), .B5(B[13]), .A6(A[14]), .B6(B[14]), .A7(A[15]),
    .B7(B[15]), .S0(S[8]), .S1(S[9]), .S2(S[10]), .S3(S[11]), .S4(S[12]), .S5(S[13]), .S6(S[14]), .S7(S[15]),
    .C8(n8_bit_2_c8));
  _8_bit u_8_bit_3 (
    .C0(n8_bit_2_c8), .A0(A[16]), .B0(B[16]), .A1(A[17]), .B1(B[17]), .A2(A[18]), .B2(B[18]), .A3(A[19]),
    .B3(B[19]), .A4(A[20]), .B4(B[20]), .A5(A[21]), .B5(B[21]), .A6(A[22]), .B6(B[22]), .A7(A[23]),
    .B7(B[23]), .S0(S[16]), .S1(S[17]), .S2(S[18]), .S3(S[19]), .S4(S[20]), .S5(S[21]), .S6(S[22]),
    .S7(S[23]), .C8(n8_bit_3_c8));
  _8_bit u_8_bit_4 (
    .C0(n8_bit_3_c8), .A0(A[24]), .B0(B[24]), .A1(A[25]), .B1(B[25]), .A2(A[26]), .B2(B[26]), .A3(A[27]),
    .B3(B[27]), .A4(A[28]), .B4(B[28]), .A5(A[29]), .B5(B[29]), .A6(A[30]), .B6(B[30]), .A7(A[31]),
    .B7(B[31]), .S0(S[24]), .S1(S[25]), .S2(S[26]), .S3(S[27]), .S4(S[28]), .S5(S[29]), .S6(S[30]), .S7(S[31]));  // open: C8
endmodule

module _30_bit (
  input  [29:0] in_1,
  input  [29:0] in_2,
  output [29:0] out_3
);

  wire n8_bit_1_c8, n8_bit_2_c8, n8_bit_3_c8;

  _8_bit u_8_bit_1 (
    .C0(1'b0), .A0(in_1[0]), .B0(in_2[0]), .A1(in_1[1]), .B1(in_2[1]), .A2(in_1[2]), .B2(in_2[2]),
    .A3(in_1[3]), .B3(in_2[3]), .A4(in_1[4]), .B4(in_2[4]), .A5(in_1[5]), .B5(in_2[5]), .A6(in_1[6]),
    .B6(in_2[6]), .A7(in_1[7]), .B7(in_2[7]), .S0(out_3[0]), .S1(out_3[1]), .S2(out_3[2]), .S3(out_3[3]),
    .S4(out_3[4]), .S5(out_3[5]), .S6(out_3[6]), .S7(out_3[7]), .C8(n8_bit_1_c8));
  _8_bit u_8_bit_2 (
    .C0(n8_bit_1_c8), .A0(in_1[8]), .B0(in_2[8]), .A1(in_1[9]), .B1(in_2[9]), .A2(in_1[10]), .B2(in_2[10]),
    .A3(in_1[11]), .B3(in_2[11]), .A4(in_1[12]), .B4(in_2[12]), .A5(in_1[13]), .B5(in_2[13]), .A6(in_1[14]),
    .B6(in_2[14]), .A7(in_1[15]), .B7(in_2[15]), .S0(out_3[8]), .S1(out_3[9]), .S2(out_3[10]),
    .S3(out_3[11]), .S4(out_3[12]), .S5(out_3[13]), .S6(out_3[14]), .S7(out_3[15]), .C8(n8_bit_2_c8));
  _8_bit u_8_bit_3 (
    .C0(n8_bit_2_c8), .A0(in_1[16]), .B0(in_2[16]), .A1(in_1[17]), .B1(in_2[17]), .A2(in_1[18]),
    .B2(in_2[18]), .A3(in_1[19]), .B3(in_2[19]), .A4(in_1[20]), .B4(in_2[20]), .A5(in_1[21]), .B5(in_2[21]),
    .A6(in_1[22]), .B6(in_2[22]), .A7(in_1[23]), .B7(in_2[23]), .S0(out_3[16]), .S1(out_3[17]),
    .S2(out_3[18]), .S3(out_3[19]), .S4(out_3[20]), .S5(out_3[21]), .S6(out_3[22]), .S7(out_3[23]),
    .C8(n8_bit_3_c8));
  _6_bit u_6_bit_1 (
    .in_1(n8_bit_3_c8), .A0(in_1[24]), .B0(in_2[24]), .A1(in_1[25]), .B1(in_2[25]), .A2(in_1[26]),
    .B2(in_2[26]), .A3(in_1[27]), .B3(in_2[27]), .A4(in_1[28]), .B4(in_2[28]), .A5(in_1[29]), .B5(in_2[29]),
    .S0(out_3[24]), .S1(out_3[25]), .S2(out_3[26]), .S3(out_3[27]), .S4(out_3[28]), .S5(out_3[29]));  // open: out_20
endmodule

module _8_bit (
  input  C0,
  input  A0,
  input  A1,
  input  A2,
  input  A3,
  input  A4,
  input  A5,
  input  A6,
  input  A7,
  input  B0,
  input  B1,
  input  B2,
  input  B3,
  input  B4,
  input  B5,
  input  B6,
  input  B7,
  output S0,
  output S1,
  output S2,
  output S3,
  output S4,
  output S5,
  output S6,
  output S7,
  output C8
);

  wire n1_bit_1_c_i_1, n1_bit_2_c_i_1, n1_bit_3_c_i_1, n1_bit_4_c_i_1, n1_bit_5_c_i_1, n1_bit_6_c_i_1,
       n1_bit_7_c_i_1;

  _1_bit u_1_bit_1 (.ai(A0), .bi(B0), .si(S0), .Ci(C0), .C_i_1(n1_bit_1_c_i_1));
  _1_bit u_1_bit_2 (.ai(A1), .bi(B1), .si(S1), .Ci(n1_bit_1_c_i_1), .C_i_1(n1_bit_2_c_i_1));
  _1_bit u_1_bit_3 (.ai(A2), .bi(B2), .si(S2), .Ci(n1_bit_2_c_i_1), .C_i_1(n1_bit_3_c_i_1));
  _1_bit u_1_bit_4 (.ai(A3), .bi(B3), .si(S3), .Ci(n1_bit_3_c_i_1), .C_i_1(n1_bit_4_c_i_1));
  _1_bit u_1_bit_5 (.ai(A4), .bi(B4), .si(S4), .Ci(n1_bit_4_c_i_1), .C_i_1(n1_bit_5_c_i_1));
  _1_bit u_1_bit_6 (.ai(A5), .bi(B5), .si(S5), .Ci(n1_bit_5_c_i_1), .C_i_1(n1_bit_6_c_i_1));
  _1_bit u_1_bit_7 (.ai(A6), .bi(B6), .si(S6), .Ci(n1_bit_6_c_i_1), .C_i_1(n1_bit_7_c_i_1));
  _1_bit u_1_bit_8 (.ai(A7), .bi(B7), .si(S7), .Ci(n1_bit_7_c_i_1), .C_i_1(C8));
endmodule

module _6_bit (
  input  in_1,
  input  A0,
  input  B0,
  input  A1,
  input  B1,
  input  A2,
  input  B2,
  input  A3,
  input  B3,
  input  A4,
  input  B4,
  input  A5,
  input  B5,
  output S0,
  output S1,
  output S2,
  output S3,
  output S4,
  output S5,
  output out_20
);

  wire n1_bit_1_c_i_1, n1_bit_2_c_i_1, n1_bit_3_c_i_1, n1_bit_4_c_i_1, n1_bit_5_c_i_1;

  _1_bit u_1_bit_1 (.ai(A0), .bi(B0), .si(S0), .Ci(in_1), .C_i_1(n1_bit_1_c_i_1));
  _1_bit u_1_bit_2 (.ai(A1), .bi(B1), .si(S1), .Ci(n1_bit_1_c_i_1), .C_i_1(n1_bit_2_c_i_1));
  _1_bit u_1_bit_3 (.ai(A2), .bi(B2), .si(S2), .Ci(n1_bit_2_c_i_1), .C_i_1(n1_bit_3_c_i_1));
  _1_bit u_1_bit_4 (.ai(A3), .bi(B3), .si(S3), .Ci(n1_bit_3_c_i_1), .C_i_1(n1_bit_4_c_i_1));
  _1_bit u_1_bit_5 (.ai(A4), .bi(B4), .si(S4), .Ci(n1_bit_4_c_i_1), .C_i_1(n1_bit_5_c_i_1));
  _1_bit u_1_bit_6 (.ai(A5), .bi(B5), .si(S5), .Ci(n1_bit_5_c_i_1), .C_i_1(out_20));
endmodule

module _1_bit (
  input  Ci,
  input  ai,
  input  bi,
  output si,
  output C_i_1
);

  wire and_1_out, and_2_out, xor_1_out;

  xor xor_1 (xor_1_out, ai, bi);
  and and_1 (and_1_out, ai, bi);
  and and_2 (and_2_out, xor_1_out, Ci);
  xor xor_2 (si, xor_1_out, Ci);
  or or_1 (C_i_1, and_1_out, and_2_out);
endmodule
